# Fritzing sketch Overall Circuit (saved by Fritzing 0.7.11b)
breadboards: 1

parts:
  Uno1 = chipKIT Uno32 [package="SIP (Single Inline) [THT]"]
  LED1 = LED - 5mm [color="Red (633nm)" package="5 mm [THT]"]
  R1 = Resistor [tolerance=±5% resistance=330 package=THT]
  S1 = Pushbutton [package="[THT]"]
  R2 = Resistor [tolerance=±5% resistance=10k package=THT]

nets:
  N1: Uno1.D7, S1.Pin_1, S1.Pin_2, R2.Pin_0
  N2: Uno1.D12, LED1.anode
  N3: Uno1.GND, R1.Pin_1, R2.Pin_1
  N4: Uno1.5V, S1.Pin_3, S1.Pin_4
  N5: LED1.cathode, R1.Pin_0

custom parts:
  chipKIT Uno32: Arduino-compatible prototyping platform
