# Fritzing sketch Circuit_test (saved by Fritzing 0.7.12b)
breadboards: 1

parts:
  Uno1 = chipKIT Uno32 [package="SIP (Single Inline) [THT]"]
  R1 = Trimmer Potentiometer [maximum_resistance=10kΩ package=THT]
  R2 = Resistor [tolerance=±5% resistance=10k package=THT]
  R3 = Resistor [tolerance=±5% resistance=10k package=THT]
  LED1 = LED - 5mm [color="Red (633nm)" package="5 mm [THT]"]
  R4 = Resistor [tolerance=±5% resistance=220 package=THT]

nets:
  N1: Uno1.GND, R1.wiper, R4.Pin_1
  N2: Uno1.D33, LED1.anode
  N3: Uno1.A0, R1.leg1, R2.Pin_1, R3.Pin_1
  N4: Uno1.5V, R2.Pin_0, R3.Pin_0
  N5: LED1.cathode, R4.Pin_0

custom parts:
  chipKIT Uno32: Arduino-compatible prototyping platform
