# Fritzing sketch Circuit (saved by Fritzing 0.7.12b)
breadboards: 1

parts:
  Uno1 = chipKIT Uno32 [package="SIP (Single Inline) [THT]"]
  S1 = Pushbutton [package="[THT]"]
  S2 = Pushbutton [package="[THT]"]
  R1 = Resistor [tolerance=±5% resistance=220 package=THT]
  R2 = Resistor [tolerance=±5% resistance=220 package=THT]
  J1 = Basic Servo

nets:
  N1: Uno1.D6, S2.Pin_3, S2.Pin_4, R2.Pin_1
  N2: Uno1.D7, S1.Pin_3, S1.Pin_4, R1.Pin_1
  N3: Uno1.D9, J1.pulse
  N4: Uno1.GND, R1.Pin_0, R2.Pin_0
  N5: Uno1.3V3, S1.Pin_1, S1.Pin_2, S2.Pin_1, S2.Pin_2

custom parts:
  chipKIT Uno32: Arduino-compatible prototyping platform
