# Fritzing sketch Circuit_test (saved by Fritzing 0.7.12b)
breadboards: 1

parts:
  Uno1 = chipKIT Uno32 [package="SIP (Single Inline) [THT]"]
  R1 = Trimmer Potentiometer [maximum_resistance=10kΩ package=THT]
  R2 = Resistor [tolerance=±5% resistance=10k package=THT]
  R3 = Resistor [tolerance=±5% resistance=10k package=THT]
  J1 = Basic Servo

nets:
  N1: Uno1.D9, J1.pulse
  GND: Uno1.GND, J1.gnd
  N2: Uno1.A0, R1.leg2, R2.Pin_0, R3.Pin_0
  N3: R2.Pin_1, R3.Pin_1, J1.vcc

custom parts:
  chipKIT Uno32: Arduino-compatible prototyping platform
